# Fritzing sketch Sketch_230727 (saved by Fritzing 0.9.3b)

parts:
  부품2 = Arduino Mega 2560 (Rev3)
  M1 = DC Motor
  M2 = DC Motor
  M3 = DC Motor
  M4 = DC Motor
  S1 = H-Bridge with L298N
  S2 = H-Bridge with L298N
  부품3 = InvenSense MPU6050
  VCC1 = Battery block 9V

nets:
  N1: 부품2.D21/SCL, 부품3.SCL
  N2: 부품2.D20/SDA, 부품3.SDA
  5V: 부품2.5V, S1.5V, 부품3.VCC
  GND: 부품2.GND, 부품3.GND
  N3: 부품2.D2_PWM, 부품3.INT
  N4: 부품2.D30, S1.IN4
  N5: 부품2.D31, S1.IN3
  N6: 부품2.D32, S1.IN1
  N7: 부품2.D33, S1.IN2
  N8: 부품2.D34, S2.IN1
  N9: 부품2.D35, S2.IN2
  N10: 부품2.D36, S2.IN3
  N11: 부품2.D37, S2.IN4
  N12: M1.pin_1, S1.M2-02
  N13: M1.pin_2, S1.M2-01
  N14: M2.pin_1, S2.M1-02
  N15: M2.pin_2, S2.M1-01
  N16: M3.pin_1, S1.M1-02
  N17: M3.pin_2, S1.M1-01
  N18: M4.pin_1, S2.M2-02
  N19: M4.pin_2, S2.M2-01
  N20: S1.12V, VCC1.+
  N21: S2.GND, VCC1.-

custom parts:
  H-Bridge with L298N: h-bridge
